# Fritzing sketch meteorStation (saved by Fritzing 0.8.7b)

parts:
  Part2 = Arduino Prototyping Shield
  R1 = Resistor [tolerance=±5% resistance=10k package=THT]
  Part4 = JeePlug experimenter's board
  Part5 = JeePlug experimenter's board
  Part6 = JeePlug experimenter's board
  S1 = Pushbutton [package="[THT]"]
  S2 = Pushbutton [package="[THT]"]
  S3 = Pushbutton [package="[THT]"]
  S4 = Pushbutton [package="[THT]"]
  S5 = Pushbutton [package="[THT]"]
  J1 = screw terminal, 3 pins
  IC1 = IC, SIP package, 3 pins [chip_label=735]
  X1 = USB Connectors [package=usb-microb]
  K1 = Relay [part_number=FRS1B-S package=THT]
  R2 = Resistor [tolerance=±5% resistance=10k package=THT]
  Part7 = JeePlug experimenter's board

nets:
  N1: Part2.A0, Part5.B5
  N2: Part2.A1, Part5.B6
  N3: Part2.A2, Part5.B4, Part5.N$8, S5.Pin_1, S5.Pin_2
  N4: Part2.A3, Part5.B2
  N5: Part2.A4, Part5.B3, Part5.N$9, S4.Pin_1, S4.Pin_2
  N6: Part2.D0(RX), X1.VBUS
  N7: Part2.D1(TX), X1.GND
  N8: Part2.D2, Part4.A4
  N9: Part2.D3, Part4.A5
  N10: Part2.D4, Part2.N$241, R2.Pin_1, Part7.A6
  N11: Part2.D5, Part2.N$418, R1.Pin_1, K1.C1, K1.C2
  N12: Part2.D6, Part4.A6
  N13: Part2.+5V, Part2.N$229, K1.B, R2.Pin_0
  N14: Part2.GND, Part2.N$247, R1.Pin_0, Part5.B1, Part6.A6, Part7.A1
  N15: Part2.D8, Part6.A1
  N16: Part2.D9, Part6.A2
  N17: Part2.D10, Part6.A3
  N18: Part2.D11, Part6.A4
  N19: Part2.D12, Part6.A5
  N20: Part4.B4, J1.pin3, IC1.pin1
  N21: Part4.B3, J1.pin2, IC1.pin2
  N22: Part4.B2, J1.pin1, IC1.pin3
  N23: Part5.A3, Part5.N$24, S1.Pin_3, S1.Pin_4
  N24: Part5.A4, Part5.N$26, S2.Pin_3, S2.Pin_4
  N25: Part5.N$7, Part5.N$18, S4.Pin_3, S4.Pin_4
  N26: Part5.N$19, Part5.N$21, S5.Pin_3, S5.Pin_4
  N27: Part5.N$27, Part5.N$30, S3.Pin_1, S3.Pin_2
  N28: Part5.N$41, Part5.N$44, S3.Pin_3, S3.Pin_4
  N29: Part5.N$47, Part5.N$50, S1.Pin_1, S1.Pin_2
  N30: Part5.N$51, Part5.N$53, S2.Pin_1, S2.Pin_2
